# Fritzing sketch bluetooth (saved by Fritzing 0.9.2b)
breadboards: 1

parts:
  Part1 = Arduino Uno (Rev3)
  Part2 = Bluetooth HC-06

nets:
  N1: Part1.D2, Part2.TXD
  N2: Part1.D3_PWM, Part2.RXD
  5V: Part1.5V, Part2.VCC
  GND: Part1.GND, Part2.GND
